// Logisim project test-class.circ as structural Verilog: 1 circuit, main circuit main
module main (
  input  in_1,
  input  in_2
);

  wire clock_1_out, clock_2_out, counter_1_q, counter_2_q, xor_1_out;

  Clock clock_1 (.out(clock_1_out));
  Clock clock_2 (.out(clock_2_out));
  Counter #(.width(1), .max('h1)) counter_1 (.Q(counter_1_q), .clk(clock_1_out));  // open: load, D, count, carry, clr
  Counter #(.width(1), .max('h1)) counter_2 (.Q(counter_2_q), .clk(clock_2_out));  // open: load, D, count, carry, clr
  xor xor_1 (xor_1_out, counter_1_q, in_1);
  LED led_1 (.in(xor_1_out));
  LED led_2 (.in(in_2));

  // Notes on the sheet:
  //   Fonction balancée
  //   Fonction constante
endmodule
