// Logisim project num-adder.circ as structural Verilog: 3 circuits, main circuit main
module main (
  input  in_1,
  input  in_2,
  input  in_3,
  input  in_4,
  input  in_5,
  input  in_6,
  output out_7,
  output out_8,
  output out_9,
  output out_10
);

  wire test1_1_out_5, test_1_out_4;

  test test_1 (.in_1(in_1), .in_2(in_4), .out_3(out_7), .out_4(test_1_out_4));
  test1 test1_1 (.in_1(test_1_out_4), .in_2(in_2), .in_3(in_5), .out_4(out_8), .out_5(test1_1_out_5));
  test1 test1_2 (.in_1(test1_1_out_5), .in_2(in_3), .in_3(in_6), .out_4(out_9), .out_5(out_10));
endmodule

module test (
  input  in_1,
  input  in_2,
  output out_3,
  output out_4
);

  xor xor_1 (out_3, in_1, in_2);
  and and_1 (out_4, in_1, in_2);
endmodule

module test1 (
  input  in_1,
  input  in_2,
  input  in_3,
  output out_4,
  output out_5
);

  wire test_1_out_3, test_1_out_4, test_2_out_4;

  test test_1 (.in_1(in_1), .in_2(in_2), .out_3(test_1_out_3), .out_4(test_1_out_4));
  test test_2 (.in_1(test_1_out_3), .in_2(in_3), .out_3(out_4), .out_4(test_2_out_4));
  or or_1 (out_5, test_2_out_4, test_1_out_4);
endmodule
